# Fritzing sketch PCB (saved by Fritzing 0.9.3b)
circuit board: 9.3cm x 3.1cm
breadboards: 1

parts:
  J1 = Piezo Speaker [part_number=buzz]
  Pro_Mini1 = Arduino Pro Mini (3.3V) [part_number=none]
  R2 = Resistor [tolerance=±5% resistance=20k package="0805 [SMD]"]
  R1 = Resistor [tolerance=±5% resistance=20k package="0805 [SMD]"]
  USB_charger1 = Micro USB charger [part_number=none]
  IRF1 = IRF7342 [chip_label=IRF7342 package=SO]
  J2 = Generic female header - 4 pins [form="♀ (female)"]
  J3 = Generic female header - 4 pins [form="♀ (female)"]
  NFC1 = NFC BM019 [part_number=1 package=SMD]
  U1 = ESP8266 WiFi Module [part_number=ESP8266]
  S1 = Toggle Switch [package=THT]

nets:
  GND: J1.pin1, Pro_Mini1.GND, R1.Pin_0, USB_charger1.GND, J2.pin4, J3.pin3, NFC1.GND, U1.GND
  N1: J1.pin2, Pro_Mini1.D9
  N2: Pro_Mini1.DTR, J2.pin1
  N3: Pro_Mini1.TXO, J2.pin3
  N4: Pro_Mini1.RXI, J2.pin2
  N5: Pro_Mini1.VCC, IRF1.S1, IRF1.S2, S1.COM
  N6: Pro_Mini1.SCK, NFC1.SCK
  N7: Pro_Mini1.MISO, NFC1.MISO
  N8: Pro_Mini1.MOSI, NFC1.MOSI
  N9: Pro_Mini1.D10, NFC1.SS
  N10: Pro_Mini1.D8, NFC1.DIN
  N11: Pro_Mini1.D7, IRF1.G1
  N12: Pro_Mini1.D4, IRF1.G2
  N13: Pro_Mini1.D3, J3.pin1, U1.TXD
  N14: Pro_Mini1.D2, J3.pin2, U1.RXD
  N15: R2.Pin_0, IRF1.D2, U1.VCC
  N16: R2.Pin_1, U1.CH_PD
  N17: R1.Pin_1, U1.GPIO_15
  N18: USB_charger1.VDD, S1.L1
  N19: IRF1.D1, NFC1.SS0, NFC1.VDD

custom parts:
  Arduino Pro Mini (3.3V): single side
  Generic female header - 4 pins: Generic female header
  Generic female header - 4 pins: Generic female header
  ESP8266 WiFi Module: Generic WiFi Module based on the ESP8266 with onboard PCB antenna and UART communications
